// Logisim project TME2.circ as structural Verilog: 6 circuits, main circuit main
module main (
  input  A,
  input  B,
  input  Cin,
  output S,
  output Cout
);

  wire and_1_out, and_2_out, xor_1_out_3;

  Xor xor_1 (.B(B), .A(A), .out_3(xor_1_out_3));
  and and_1 (and_1_out, Cin, xor_1_out_3);
  and and_2 (and_2_out, A, B);
  or or_1 (Cout, and_1_out, and_2_out);
  Xor xor_2 (.B(Cin), .A(xor_1_out_3), .out_3(S));
endmodule

module Xor (
  input  B,
  input  A,
  output out_3
);

  wire and_1_out, and_2_out, not_1_out, not_2_out;

  not not_1 (not_1_out, B);
  not not_2 (not_2_out, A);
  and and_1 (and_1_out, not_1_out, A);
  and and_2 (and_2_out, B, not_2_out);
  or or_1 (out_3, and_1_out, and_2_out);
endmodule

module add1 (
  input  A,
  input  B,
  input  Cin,
  output S,
  output Cout
);

  wire and_1_out, and_2_out, xor_1_out_3;

  Xor xor_1 (.B(B), .A(A), .out_3(xor_1_out_3));
  and and_1 (and_1_out, Cin, xor_1_out_3);
  and and_2 (and_2_out, A, B);
  or or_1 (Cout, and_1_out, and_2_out);
  Xor xor_2 (.B(Cin), .A(xor_1_out_3), .out_3(S));
endmodule

module add4 (
  input  A0,
  input  B0,
  input  A1,
  input  B1,
  input  A2,
  input  B2,
  input  A,
  input  B,
  output S0,
  output S1,
  output S2,
  output S3,
  output Cout
);

  wire and_1_out, and_2_out, and_3_out, and_4_out, and_5_out, and_6_out, and_7_out, or_1_out, or_2_out,
       xor_2_out_3, xor_4_out_3, xor_6_out_3;

  and and_1 (and_1_out, A0, B0);
  Xor xor_1 (.B(B0), .A(A0), .out_3(S0));
  Xor xor_2 (.B(B1), .A(A1), .out_3(xor_2_out_3));
  and and_2 (and_2_out, and_1_out, xor_2_out_3);
  or or_1 (or_1_out, and_2_out, and_3_out);
  Xor xor_3 (.B(and_1_out), .A(xor_2_out_3), .out_3(S1));
  and and_3 (and_3_out, A1, B1);
  and and_4 (and_4_out, or_1_out, xor_4_out_3);
  Xor xor_4 (.B(B2), .A(A2), .out_3(xor_4_out_3));
  and and_5 (and_5_out, A2, B2);
  or or_2 (or_2_out, and_4_out, and_5_out);
  Xor xor_5 (.B(or_1_out), .A(xor_4_out_3), .out_3(S2));
  and and_6 (and_6_out, or_2_out, xor_6_out_3);
  Xor xor_6 (.B(B), .A(A), .out_3(xor_6_out_3));
  and and_7 (and_7_out, A, B);
  or or_3 (Cout, and_6_out, and_7_out);
  Xor xor_7 (.B(or_2_out), .A(xor_6_out_3), .out_3(S3));
endmodule

module ALU_V1 (
  input  ALUOP,
  input  X3,
  input  X2,
  input  X1,
  input  X0,
  input  Y3,
  input  Y2,
  input  Y1,
  input  Y0,
  output S3,
  output S2,
  output S1,
  output S0,
  output Cout
);

  wire add4_1_s0, add4_1_s1, add4_1_s2, add4_1_s3, add4_2_cout, add4_2_s0, add4_2_s1, add4_2_s2, add4_2_s3,
       add4_3_cout, add4_3_s0, add4_3_s1, add4_3_s2, add4_3_s3, and_1_out, and_2_out, and_3_out, and_4_out,
       and_5_out, and_6_out, and_7_out, and_8_out, and_9_out, and_10_out, not_1_out, not_2_out, not_3_out,
       not_4_out, not_5_out;

  not not_1 (not_1_out, Y0);
  not not_2 (not_2_out, Y1);
  not not_3 (not_3_out, Y2);
  not not_4 (not_4_out, Y3);
  add4 add4_1 (
    .S0(add4_1_s0), .S1(add4_1_s1), .S2(add4_1_s2), .S3(add4_1_s3), .A0(not_1_out), .B0(1'b1),
    .A1(not_2_out), .B1(1'b0), .A2(not_3_out), .B2(1'b0), .A(not_4_out), .B(1'b0));  // open: Cout
  add4 add4_2 (
    .S0(add4_2_s0), .S1(add4_2_s1), .S2(add4_2_s2), .S3(add4_2_s3), .Cout(add4_2_cout), .A0(X0), .B0(Y0),
    .A1(X1), .B1(Y1), .A2(X2), .B2(Y2), .A(X3), .B(Y3));
  add4 add4_3 (
    .S0(add4_3_s0), .S1(add4_3_s1), .S2(add4_3_s2), .S3(add4_3_s3), .Cout(add4_3_cout), .A0(X0),
    .B0(add4_1_s0), .A1(X1), .B1(add4_1_s1), .A2(X2), .B2(add4_1_s2), .A(X3), .B(add4_1_s3));
  not not_5 (not_5_out, ALUOP);
  and and_1 (and_1_out, not_5_out, add4_2_s3);
  and and_2 (and_2_out, ALUOP, add4_3_s3);
  and and_3 (and_3_out, not_5_out, add4_2_s2);
  and and_4 (and_4_out, ALUOP, add4_3_s2);
  and and_5 (and_5_out, add4_2_s1, not_5_out);
  and and_6 (and_6_out, add4_3_s1, ALUOP);
  and and_7 (and_7_out, add4_2_s0, not_5_out);
  and and_8 (and_8_out, add4_3_s0, ALUOP);
  and and_9 (and_9_out, add4_2_cout, not_5_out);
  and and_10 (and_10_out, ALUOP, add4_3_cout);
  or or_1 (S3, and_1_out, and_2_out);
  or or_2 (S1, and_5_out, and_6_out);
  or or_3 (S0, and_7_out, and_8_out);
  or or_4 (Cout, and_9_out, and_10_out);
  or or_5 (S2, and_3_out, and_4_out);
endmodule

module ALU_v1 (
  input  A0,
  input  A1,
  input  A2,
  input  A,
  input  B0,
  input  B1,
  input  B2,
  input  B,
  output S0,
  output S1,
  output S2,
  output S3
);

  wire and_1_out, and_2_out, and_3_out, and_4_out, and_5_out, and_6_out, and_7_out, or_1_out, or_2_out,
       or_3_out, xor_2_out_3, xor_4_out_3, xor_6_out_3;

  Xor xor_1 (.B(B0), .A(A0), .out_3(S0));
  and and_1 (and_1_out, B0, A0);
  Xor xor_2 (.B(B1), .A(A1), .out_3(xor_2_out_3));
  and and_2 (and_2_out, and_1_out, xor_2_out_3);
  or or_1 (or_1_out, and_2_out, and_3_out);
  Xor xor_3 (.B(and_1_out), .A(xor_2_out_3), .out_3(S1));
  and and_3 (and_3_out, A1, B1);
  and and_4 (and_4_out, or_1_out, xor_4_out_3);
  Xor xor_4 (.B(B2), .A(A2), .out_3(xor_4_out_3));
  and and_5 (and_5_out, A2, B2);
  or or_2 (or_2_out, and_4_out, and_5_out);
  Xor xor_5 (.B(or_1_out), .A(xor_4_out_3), .out_3(S2));
  and and_6 (and_6_out, or_2_out, xor_6_out_3);
  Xor xor_6 (.B(B), .A(A), .out_3(xor_6_out_3));
  and and_7 (and_7_out, A, B);
  or or_3 (or_3_out, and_6_out, and_7_out);
  Xor xor_7 (.B(or_2_out), .A(xor_6_out_3), .out_3(S3));
endmodule
