// Logisim project mon_xor.circ as structural Verilog: 5 circuits, main circuit main
module main (
  input  a,
  input  b,
  input  in_3,
  input  in_4,
  input  a_2,
  input  b_2,
  output out_7,
  output out_8,
  output out_9
);

  wire and_2_out, and_3_out, not_1_out, not_2_out, not_3_out;

  not not_1 (not_1_out, b);
  not not_2 (not_2_out, a_2);
  not not_3 (not_3_out, b_2);
  and and_1 (out_7, a, not_1_out);
  or or_1 (out_8, in_3, in_4);
  and and_2 (and_2_out, not_2_out, b_2);
  and and_3 (and_3_out, a_2, not_3_out);
  or or_2 (out_9, and_2_out, and_3_out);
endmodule

module mux2 (
  input  e0,
  input  i,
  input  e1,
  output out_4
);

  wire and_1_out, and_2_out, not_1_out;

  not not_1 (not_1_out, i);
  and and_1 (and_1_out, not_1_out, e0);
  and and_2 (and_2_out, i, e1);
  or or_1 (out_4, and_1_out, and_2_out);
endmodule

module mon_xor (
  input  a,
  input  b,
  output out_3
);

  wire and_1_out, and_2_out, not_1_out, not_2_out;

  not not_1 (not_1_out, a);
  not not_2 (not_2_out, b);
  and and_1 (and_1_out, not_1_out, b);
  and and_2 (and_2_out, a, not_2_out);
  or or_1 (out_3, and_1_out, and_2_out);
endmodule

module mux2_4bits (
  input  in_1,
  input  A1,
  input  B1,
  input  A2,
  input  B2,
  input  A3,
  input  B3,
  input  A4,
  input  B4,
  output S1,
  output S2,
  output S3,
  output S4
);

  mux2 mux2_1 (.e0(A1), .i(in_1), .e1(B1), .out_4(S1));
  mux2 mux2_2 (.e0(A2), .i(in_1), .e1(B2), .out_4(S2));
  mux2 mux2_3 (.e0(A3), .i(in_1), .e1(B3), .out_4(S3));
  mux2 mux2_4 (.e0(A4), .i(in_1), .e1(B4), .out_4(S4));
endmodule

module mux4 (
  input  in_1,
  input  in_2,
  input  in_3,
  input  in_4,
  input  in_5,
  input  in_6,
  output out_7
);

  wire mux2_1_out_4, mux2_2_out_4;

  mux2 mux2_1 (.e0(in_3), .i(in_1), .e1(in_4), .out_4(mux2_1_out_4));
  mux2 mux2_2 (.e0(in_5), .i(in_1), .e1(in_6), .out_4(mux2_2_out_4));
  mux2 mux2_3 (.e0(mux2_1_out_4), .i(in_2), .e1(mux2_2_out_4), .out_4(out_7));
endmodule
